# Fritzing sketch etch-a-sketch (saved by Fritzing 0.9.2b)
breadboards: 1

parts:
  Part1 = Arduino Uno (Rev3)
  R1 = Rotary Potentiometer (Small) [maximum_resistance=10kΩ package=THT]
  R2 = Rotary Potentiometer (Small) [maximum_resistance=10kΩ package=THT]
  S1 = Pushbutton [package="[THT]"]
  R3 = Resistor [tolerance=±5% resistance=10k package=THT]

nets:
  N1: Part1.A0, R2.wiper
  N2: Part1.A2, R1.wiper
  N3: Part1.D2, S1.Pin_1, S1.Pin_2, R3.Pin_0
  N4: Part1.5V, R1.leg1, R2.leg1, S1.Pin_3, S1.Pin_4
  N5: Part1.GND, R1.leg2, R2.leg2, R3.Pin_1
